// Logisim project ControlUnit.circ as structural Verilog: 2 circuits, main circuit ControlUnit
module ControlUnit (
  input  WAIT_PIN,
  input  [31:0] OP,
  input  CLOCK,
  output WR_PC,
  output WR_RD,
  output RD_DEST,
  output WR_IR,
  output SEL_REG,
  output [1:0] OP_Y_SEL,
  output [3:0] OP_ALU,
  output WR_SR,
  output SEL_D,
  output WR_AR,
  output [1:0] OP_ABI,
  output [2:0] OP_DBI,
  output EN_D,
  output EN_A,
  output RD,
  output WR
);

  wire multiplexer_2_out;
  wire [1:0] rom_1_data_3, rom_1_data_5;
  wire [2:0] rom_1_data_6;
  wire [3:0] rom_1_data_4;
  wire [15:0] multiplexer_1_out, optoaddr_1_nextop_addr, register_1_q, rom_1_data;
  wire [63:0] rom_1_data_2;

  Register #(.width(16)) register_1 (.D(rom_1_data), .en(1'b1), .clk(CLOCK), .Q(register_1_q));  // open: clr
  OpToAddr optoaddr_1 (.OP(OP), .NextOp_Addr(optoaddr_1_nextop_addr));
  Multiplexer #(.width(16)) multiplexer_1 (
    .in0(register_1_q), .in1(optoaddr_1_nextop_addr), .out(multiplexer_1_out), .sel(multiplexer_2_out));
  Multiplexer multiplexer_2 (.in0(1'b0), .in1(rom_1_data_2[23]), .out(multiplexer_2_out), .sel(1'b1));
  ROM #(.addrWidth(16), .dataWidth(64)) rom_1 (
    .addr(multiplexer_1_out),
    .data({rom_1_data_2[63:40], rom_1_data, rom_1_data_2[23:19], rom_1_data_6, rom_1_data_5, rom_1_data_2[13:11], rom_1_data_4, rom_1_data_3, rom_1_data_2[4:0]}));
  Multiplexer multiplexer_3 (.in0(rom_1_data_2[0]), .in1(1'b0), .out(WR_PC), .sel(WAIT_PIN));
  Multiplexer multiplexer_4 (.in0(rom_1_data_2[1]), .in1(1'b0), .out(WR_RD), .sel(WAIT_PIN));
  Multiplexer multiplexer_5 (.in0(rom_1_data_2[2]), .in1(1'b0), .out(RD_DEST), .sel(WAIT_PIN));
  Multiplexer multiplexer_6 (.in0(rom_1_data_2[3]), .in1(1'b1), .out(WR_IR), .sel(WAIT_PIN));
  Multiplexer multiplexer_7 (.in0(rom_1_data_2[4]), .in1(1'b0), .out(SEL_REG), .sel(WAIT_PIN));
  Multiplexer #(.width(2)) multiplexer_8 (.in0(rom_1_data_3), .in1(2'b00), .out(OP_Y_SEL), .sel(WAIT_PIN));
  Multiplexer #(.width(4)) multiplexer_9 (.in0(rom_1_data_4), .in1(4'b0000), .out(OP_ALU), .sel(WAIT_PIN));
  Multiplexer multiplexer_10 (.in0(rom_1_data_2[11]), .in1(1'b0), .out(WR_SR), .sel(WAIT_PIN));
  Multiplexer multiplexer_11 (.in0(rom_1_data_2[12]), .in1(1'b1), .out(SEL_D), .sel(WAIT_PIN));
  Multiplexer multiplexer_12 (.in0(rom_1_data_2[13]), .in1(1'b0), .out(WR_AR), .sel(WAIT_PIN));
  Multiplexer #(.width(2)) multiplexer_13 (.in0(rom_1_data_5), .in1(2'b00), .out(OP_ABI), .sel(WAIT_PIN));
  Multiplexer #(.width(3)) multiplexer_14 (.in0(rom_1_data_6), .in1(3'b000), .out(OP_DBI), .sel(WAIT_PIN));
  Multiplexer multiplexer_15 (.in0(rom_1_data_2[19]), .in1(1'b0), .out(EN_D), .sel(WAIT_PIN));
  Multiplexer multiplexer_16 (.in0(rom_1_data_2[20]), .in1(1'b1), .out(EN_A), .sel(WAIT_PIN));
  Multiplexer multiplexer_17 (.in0(rom_1_data_2[21]), .in1(1'b1), .out(RD), .sel(WAIT_PIN));
  Multiplexer multiplexer_18 (.in0(rom_1_data_2[22]), .in1(1'b0), .out(WR), .sel(WAIT_PIN));

  // Notes on the sheet:
  //   Init
endmodule

module OpToAddr (
  input  [31:0] OP,
  output [15:0] NextOp_Addr
);

  ROM #(.dataWidth(16)) rom_1 (.addr(OP[31:24]), .data(NextOp_Addr));
endmodule
