// Logisim project DBI.circ as structural Verilog: 6 circuits, main circuit OP_DBI_Select
module DBI (
  input  [31:0] RAWIN,
  input  [1:0] A1A0,
  input  [2:0] OP,
  input  [31:0] DOUT,
  output [31:0] DIN,
  output [31:0] RAWOUT
);

  wire op_dbi_select_1_o1, op_dbi_select_1_o2, op_dbi_select_1_o3, op_dbi_select_1_o4, op_dbi_select_1_o5,
       op_dbi_select_1_o6a, op_dbi_select_1_o6b, op_dbi_select_1_o6c, op_dbi_select_1_o6d,
       op_dbi_select_1_o7a, op_dbi_select_1_o7b, op_dbi_select_1_o7c, op_dbi_select_1_o7d,
       op_dbi_select_1_o8, op_dbi_select_1_o9a, op_dbi_select_1_o9b, op_dbi_select_1_o10a,
       op_dbi_select_1_o10b, op_dbi_select_1_o10c, op_dbi_select_1_o10d;

  OP_DBI_Select op_dbi_select_1 (
    .A1A0(A1A0), .OP(OP), .O1(op_dbi_select_1_o1), .O2(op_dbi_select_1_o2), .O3(op_dbi_select_1_o3),
    .O4(op_dbi_select_1_o4), .O5(op_dbi_select_1_o5), .O6a(op_dbi_select_1_o6a), .O6b(op_dbi_select_1_o6b),
    .O6c(op_dbi_select_1_o6c), .O6d(op_dbi_select_1_o6d), .O7a(op_dbi_select_1_o7a),
    .O7b(op_dbi_select_1_o7b), .O7c(op_dbi_select_1_o7c), .O7d(op_dbi_select_1_o7d), .O8(op_dbi_select_1_o8),
    .O9a(op_dbi_select_1_o9a), .O9b(op_dbi_select_1_o9b), .O10a(op_dbi_select_1_o10a),
    .O10b(op_dbi_select_1_o10b), .O10c(op_dbi_select_1_o10c), .O10d(op_dbi_select_1_o10d));
  assign DIN = op_dbi_select_1_o1 ? RAWIN : 32'bz;  // Controlled_Buffer controlled_buffer_1
  assign RAWOUT = op_dbi_select_1_o8 ? DOUT : 32'bz;  // Controlled_Buffer controlled_buffer_2
  HALF_WORD_Lee half_word_lee_1 (
    .RAWIN(RAWIN), .I2(op_dbi_select_1_o2), .I3(op_dbi_select_1_o3), .I4(op_dbi_select_1_o4),
    .I5(op_dbi_select_1_o5), .DIN(DIN));
  BYTE_Lee byte_lee_1 (
    .RAWIN(RAWIN), .I6a(op_dbi_select_1_o6a), .I6b(op_dbi_select_1_o6b), .I6c(op_dbi_select_1_o6c),
    .I6d(op_dbi_select_1_o6d), .I7a(op_dbi_select_1_o7a), .I7b(op_dbi_select_1_o7b),
    .I7c(op_dbi_select_1_o7c), .I7d(op_dbi_select_1_o7d), .DIN(DIN));
  HALF_WORD_Escribe half_word_escribe_1 (
    .DOUT(DOUT), .I1(op_dbi_select_1_o9a), .I2(op_dbi_select_1_o9b), .RAWOUT(RAWOUT));
  BYTE_Escribe byte_escribe_1 (
    .DOUT(DOUT), .I10a(op_dbi_select_1_o10a), .I10b(op_dbi_select_1_o10b), .I10c(op_dbi_select_1_o10c),
    .I10d(op_dbi_select_1_o10d), .RAWOUT(RAWOUT));
endmodule

module OP_DBI_Select (
  input  [1:0] A1A0,
  input  [2:0] OP,
  output O1,
  output O2,
  output O3,
  output O4,
  output O5,
  output O6a,
  output O6b,
  output O6c,
  output O6d,
  output O7a,
  output O7b,
  output O7c,
  output O7d,
  output O8,
  output O9a,
  output O9b,
  output O10a,
  output O10b,
  output O10c,
  output O10d
);

  wire and_1_out, and_2_out, and_3_out, and_4_out, and_5_out, and_6_out, and_7_out, and_8_out, and_9_out,
       and_10_out, and_11_out, and_12_out, and_13_out, and_14_out, and_15_out, and_16_out, and_17_out,
       and_18_out, and_19_out, and_20_out, and_21_out, and_22_out, and_23_out, and_24_out, and_25_out,
       and_26_out, and_27_out, and_28_out, and_29_out, and_30_out, and_31_out, and_32_out, and_33_out,
       and_34_out, and_35_out, and_36_out, and_37_out, and_38_out, and_39_out, and_40_out, not_1_out,
       not_2_out, not_3_out, not_4_out, not_5_out;

  not not_1 (not_1_out, OP[2]);
  not not_2 (not_2_out, OP[1]);
  not not_3 (not_3_out, OP[0]);
  not not_4 (not_4_out, A1A0[1]);
  not not_5 (not_5_out, A1A0[0]);
  and and_1 (and_1_out, not_1_out, not_2_out);
  and and_2 (and_2_out, not_3_out, not_4_out, not_5_out);
  and and_3 (and_3_out, not_1_out, not_2_out);
  and and_4 (and_4_out, OP[0], not_4_out, not_5_out);
  and and_5 (and_5_out, not_1_out, not_2_out);
  and and_6 (and_6_out, OP[0], A1A0[1], not_5_out);
  and and_7 (and_7_out, not_1_out, OP[1]);
  and and_8 (and_8_out, not_3_out, not_4_out, not_5_out);
  and and_9 (and_9_out, not_1_out, OP[1]);
  and and_10 (and_10_out, not_3_out, A1A0[1], not_5_out);
  and and_11 (and_11_out, not_1_out, OP[1]);
  and and_12 (and_12_out, OP[0], not_4_out, not_5_out);
  and and_13 (and_13_out, not_1_out, OP[1]);
  and and_14 (and_14_out, OP[0], not_4_out, A1A0[0]);
  and and_15 (and_15_out, not_1_out, OP[1]);
  and and_16 (and_16_out, OP[0], A1A0[1], not_5_out);
  and and_17 (and_17_out, not_1_out, OP[1]);
  and and_18 (and_18_out, OP[0], A1A0[1], A1A0[0]);
  and and_19 (and_19_out, OP[2], not_2_out);
  and and_20 (and_20_out, not_3_out, not_4_out, not_5_out);
  and and_21 (and_21_out, OP[2], not_2_out);
  and and_22 (and_22_out, not_3_out, not_4_out, A1A0[0]);
  and and_23 (and_23_out, OP[2], not_2_out);
  and and_24 (and_24_out, not_3_out, A1A0[1], not_5_out);
  and and_25 (and_25_out, OP[2], not_2_out);
  and and_26 (and_26_out, not_3_out, A1A0[1], A1A0[0]);
  and and_27 (and_27_out, OP[2], not_2_out);
  and and_28 (and_28_out, OP[0], not_4_out, not_5_out);
  and and_29 (and_29_out, OP[2], OP[1]);
  and and_30 (and_30_out, not_3_out, not_4_out, not_5_out);
  and and_31 (and_31_out, OP[2], not_1_out);
  and and_32 (and_32_out, not_3_out, A1A0[1], not_5_out);
  and and_33 (and_33_out, OP[2], OP[1]);
  and and_34 (and_34_out, OP[0], not_4_out, not_5_out);
  and and_35 (and_35_out, OP[2], OP[1]);
  and and_36 (and_36_out, OP[0], not_4_out, A1A0[0]);
  and and_37 (and_37_out, OP[2], OP[1]);
  and and_38 (and_38_out, OP[0], A1A0[1], not_5_out);
  and and_39 (and_39_out, OP[2], OP[1]);
  and and_40 (and_40_out, OP[0], A1A0[1], A1A0[0]);
  and and_41 (O1, and_1_out, and_2_out);
  and and_42 (O2, and_3_out, and_4_out);
  and and_43 (O3, and_5_out, and_6_out);
  and and_44 (O4, and_7_out, and_8_out);
  and and_45 (O5, and_9_out, and_10_out);
  and and_46 (O6a, and_11_out, and_12_out);
  and and_47 (O6b, and_13_out, and_14_out);
  and and_48 (O6c, and_15_out, and_16_out);
  and and_49 (O6d, and_17_out, and_18_out);
  and and_50 (O7a, and_19_out, and_20_out);
  and and_51 (O7b, and_21_out, and_22_out);
  and and_52 (O7c, and_23_out, and_24_out);
  and and_53 (O7d, and_25_out, and_26_out);
  and and_54 (O8, and_27_out, and_28_out);
  and and_55 (O9a, and_29_out, and_30_out);
  and and_56 (O9b, and_31_out, and_32_out);
  and and_57 (O10a, and_33_out, and_34_out);
  and and_58 (O10b, and_35_out, and_36_out);
  and and_59 (O10c, and_37_out, and_38_out);
  and and_60 (O10d, and_39_out, and_40_out);
endmodule

module HALF_WORD_Lee (
  input  [31:0] RAWIN,
  input  I2,
  input  I3,
  input  I4,
  input  I5,
  output [31:0] DIN
);

  wire [31:31] not_1_out, not_2_out;

  not not_1 (not_1_out[31], I2);
  not not_2 (not_2_out[31], I3);
  assign DIN = I2 ? {{16{not_1_out[31]}}, RAWIN[31:16]} : 32'bz;  // Controlled_Buffer controlled_buffer_1
  assign DIN = I3 ? {{16{not_2_out[31]}}, RAWIN[15:0]} : 32'bz;  // Controlled_Buffer controlled_buffer_2
  assign DIN = I4 ? {{17{RAWIN[31]}}, RAWIN[30:16]} : 32'bz;  // Controlled_Buffer controlled_buffer_3
  assign DIN = I5 ? {{17{RAWIN[15]}}, RAWIN[14:0]} : 32'bz;  // Controlled_Buffer controlled_buffer_4
endmodule

module HALF_WORD_Escribe (
  input  [31:0] DOUT,
  input  I1,
  input  I2,
  output [31:0] RAWOUT
);

  wire [31:31] not_1_out, not_2_out;

  not not_1 (not_1_out[31], I1);
  not not_2 (not_2_out[31], I2);
  assign RAWOUT = I1 ? {{16{not_1_out[31]}}, DOUT[31:16]} : 32'bz;  // Controlled_Buffer controlled_buffer_1
  assign RAWOUT = I1 ? {{16{not_2_out[31]}}, DOUT[15:0]} : 32'bz;  // Controlled_Buffer controlled_buffer_2
endmodule

module BYTE_Lee (
  input  [31:0] RAWIN,
  input  I6a,
  input  I6b,
  input  I6c,
  input  I6d,
  input  I7a,
  input  I7b,
  input  I7c,
  input  I7d,
  output [31:0] DIN
);

  wire [31:31] not_1_out, not_2_out, not_3_out, not_4_out;

  not not_1 (not_1_out[31], I6a);
  not not_2 (not_2_out[31], I6b);
  not not_3 (not_3_out[31], I6c);
  not not_4 (not_4_out[31], I6d);
  assign DIN = I6a ? {{24{not_1_out[31]}}, RAWIN[31:24]} : 32'bz;  // Controlled_Buffer controlled_buffer_1
  assign DIN = I6b ? {{24{not_2_out[31]}}, RAWIN[23:16]} : 32'bz;  // Controlled_Buffer controlled_buffer_2
  assign DIN = I6c ? {{24{not_3_out[31]}}, RAWIN[15:8]} : 32'bz;  // Controlled_Buffer controlled_buffer_3
  assign DIN = I6d ? {{24{not_4_out[31]}}, RAWIN[7:0]} : 32'bz;  // Controlled_Buffer controlled_buffer_4
  assign DIN = I7a ? {{25{RAWIN[31]}}, RAWIN[30:24]} : 32'bz;  // Controlled_Buffer controlled_buffer_5
  assign DIN = I7b ? {{25{RAWIN[23]}}, RAWIN[22:16]} : 32'bz;  // Controlled_Buffer controlled_buffer_6
  assign DIN = I7c ? {{25{RAWIN[15]}}, RAWIN[14:8]} : 32'bz;  // Controlled_Buffer controlled_buffer_7
  assign DIN = I7d ? {{25{RAWIN[7]}}, RAWIN[6:0]} : 32'bz;  // Controlled_Buffer controlled_buffer_8
endmodule

module BYTE_Escribe (
  input  [31:0] DOUT,
  input  I10a,
  input  I10b,
  input  I10c,
  input  I10d,
  output [31:0] RAWOUT
);

  wire [31:31] not_1_out, not_2_out, not_3_out, not_4_out;

  not not_1 (not_1_out[31], I10a);
  not not_2 (not_2_out[31], I10b);
  not not_3 (not_3_out[31], I10c);
  not not_4 (not_4_out[31], I10d);
  assign RAWOUT = I10a ? {{24{not_1_out[31]}}, DOUT[31:24]} : 32'bz;  // Controlled_Buffer controlled_buffer_1
  assign RAWOUT = I10b ? {{24{not_2_out[31]}}, DOUT[23:16]} : 32'bz;  // Controlled_Buffer controlled_buffer_2
  assign RAWOUT = I10c ? {{24{not_3_out[31]}}, DOUT[15:8]} : 32'bz;  // Controlled_Buffer controlled_buffer_3
  assign RAWOUT = I10d ? {{24{not_4_out[31]}}, DOUT[7:0]} : 32'bz;  // Controlled_Buffer controlled_buffer_4
endmodule
