// Logisim project M32.circ as structural Verilog: 61 circuits, main circuit main
module main (
);

  wire clock_1_out, comparator_1_eq, m32_1_rd, m32_1_wr, quadbyteram_1_p2;
  wire [3:0] m32_1_beout;
  wire [6:0] undriven;
  wire [29:0] m32_1_aout;
  wire [31:0] i30to32_1_outpt, m32_1_rawout, quadbyteram_1_p6;

  Clock clock_1 (.out(clock_1_out));
  I30to32 i30to32_1 (.INPT(m32_1_aout), .OUTPT(i30to32_1_outpt));
  M32 m32_1 (
    .WT(quadbyteram_1_p2), .CLK(clock_1_out), .RAWIN(quadbyteram_1_p6), .AOUT(m32_1_aout),
    .BEOUT(m32_1_beout), .RAWOUT(m32_1_rawout), .RD(m32_1_rd), .WR(m32_1_wr));
  // QuadByteRam quadbyteram_1: pin names not known; wires that end beside it: clock_1_out, quadbyteram_1_p2, m32_1_rd, m32_1_wr, m32_1_rawout, quadbyteram_1_p6, m32_1_beout, i30to32_1_outpt
  TTY tty_1 (.data(undriven), .clk(clock_1_out), .we(comparator_1_eq), .clr(1'b0));
  // DefinedOutputSplitter32 definedoutputsplitter32_1: pin names not known; wires that end beside it: m32_1_rawout
  Comparator #(.width(32)) comparator_1 (.a(32'h8000000), .b(i30to32_1_outpt), .eq(comparator_1_eq));  // open: gt, lt

  // Notes on the sheet:
  //   Address
  //   Data Bus (input)
  //   Data Bus (output)
  //   Control (CLK)
  //   Control (WAIT)
  //   Control (Write)
  //   Control (Read)
  //   Control (palabra)
endmodule

module EjemploTeclado (
);

  wire clear, clock_1_out, comparator_1_eq, comparator_2_eq, comparator_3_eq, m32_1_rd, m32_1_wr,
       quadbyteram_1_p2, read;
  wire [3:0] m32_1_beout;
  wire [6:0] keyboard_1_data, undriven;
  wire [7:7] keyboard_1_avail;
  wire [29:0] m32_1_aout;
  wire [31:0] controlled_buffer_2_out, i30to32_1_outpt, m32_1_rawout, quadbyteram_1_p6;

  Clock clock_1 (.out(clock_1_out));
  I30to32 i30to32_1 (.INPT(m32_1_aout), .OUTPT(i30to32_1_outpt));
  M32 m32_1 (
    .WT(quadbyteram_1_p2), .CLK(clock_1_out), .RAWIN(quadbyteram_1_p6), .AOUT(m32_1_aout),
    .BEOUT(m32_1_beout), .RAWOUT(m32_1_rawout), .RD(m32_1_rd), .WR(m32_1_wr));
  // QuadByteRam quadbyteram_1: pin names not known; wires that end beside it: clock_1_out, quadbyteram_1_p2, m32_1_rd, m32_1_wr, m32_1_rawout, quadbyteram_1_p6, m32_1_beout, i30to32_1_outpt
  TTY tty_1 (.data(undriven), .clk(clock_1_out), .we(comparator_1_eq), .clr(1'b0));
  // DefinedOutputSplitter32 definedoutputsplitter32_1: pin names not known; wires that end beside it: m32_1_rawout
  Comparator #(.width(32)) comparator_1 (.a(32'h8000000), .b(i30to32_1_outpt), .eq(comparator_1_eq));  // open: gt, lt
  Keyboard keyboard_1 (.clk(clock_1_out), .re(read), .clr(clear), .avail(keyboard_1_avail[7]), .data(keyboard_1_data));
  Comparator #(.width(32)) comparator_2 (.a(32'h9000000), .b(i30to32_1_outpt), .eq(comparator_2_eq));  // open: gt, lt
  assign quadbyteram_1_p6 = comparator_2_eq ? {{24{1'b0}}, keyboard_1_avail[7], keyboard_1_data} : 32'bz;  // Controlled_Buffer controlled_buffer_1
  Comparator #(.width(32)) comparator_3 (.a(32'h10000000), .b(i30to32_1_outpt), .eq(comparator_3_eq));  // open: gt, lt
  assign controlled_buffer_2_out = comparator_3_eq ? m32_1_rawout : 32'bz;  // Controlled_Buffer controlled_buffer_2
  // DefinedOutputSplitter32 definedoutputsplitter32_2: pin names not known; wires that end beside it: controlled_buffer_2_out, read, clear, i30to32_1_outpt, quadbyteram_1_p6, m32_1_rawout, clock_1_out, quadbyteram_1_p2, m32_1_wr

  // Notes on the sheet:
  //   Address
  //   Data Bus (input)
  //   Data Bus (output)
  //   Control (CLK)
  //   Control (WAIT)
  //   Control (Write)
  //   Control (Read)
  //   Control (palabra)
endmodule

module EjercicioPastillas (
);

  wire CLK, m32_1_rd, m32_1_wr, ramstick_1_p2, ramstick_3_p2, sel2_1_out_2, sel4_1_out_2;
  wire [29:0] m32_1_aout;
  wire [31:0] controlled_buffer_1_out, i30to32_1_outpt, m32_1_rawout, ramstick_1_p6, ramstick_2_p6,
       ramstick_3_p6, ramstick_4_p6;

  M32 m32_1 (
    .CLK(CLK), .RAWIN(controlled_buffer_1_out), .AOUT(m32_1_aout), .RAWOUT(m32_1_rawout), .RD(m32_1_rd),
    .WR(m32_1_wr));  // open: WT, BEOUT
  Clock clock_1 (.out(CLK));
  I30to32 i30to32_1 (.INPT(m32_1_aout), .OUTPT(i30to32_1_outpt));
  // RamStick ramstick_1: pin names not known; wires that end beside it: m32_1_rd, ramstick_1_p2, m32_1_wr, m32_1_rawout, i30to32_1_outpt, ramstick_1_p6, CLK
  SEL1 sel1_1 (.in_1(i30to32_1_outpt), .out_2(ramstick_1_p2));
  assign controlled_buffer_1_out = ramstick_1_p2 ? ramstick_1_p6 : 32'bz;  // Controlled_Buffer controlled_buffer_1
  SEL2 sel2_1 (.in_1(i30to32_1_outpt), .out_2(sel2_1_out_2));
  // RamStick ramstick_2: pin names not known; wires that end beside it: m32_1_rd, sel2_1_out_2, m32_1_wr, m32_1_rawout, i30to32_1_outpt, ramstick_2_p6, CLK
  assign controlled_buffer_1_out = sel2_1_out_2 ? ramstick_2_p6 : 32'bz;  // Controlled_Buffer controlled_buffer_2
  // RamStick ramstick_3: pin names not known; wires that end beside it: m32_1_rd, ramstick_3_p2, m32_1_wr, m32_1_rawout, i30to32_1_outpt, ramstick_3_p6, CLK
  SEL3 sel3_1 (.in_1(i30to32_1_outpt), .out_2(ramstick_3_p2));
  assign controlled_buffer_1_out = ramstick_3_p2 ? ramstick_3_p6 : 32'bz;  // Controlled_Buffer controlled_buffer_3
  SEL4 sel4_1 (.in_1(i30to32_1_outpt), .out_2(sel4_1_out_2));
  // RamStick ramstick_4: pin names not known; wires that end beside it: m32_1_rd, sel4_1_out_2, m32_1_wr, m32_1_rawout, i30to32_1_outpt, ramstick_4_p6, CLK
  assign controlled_buffer_1_out = sel4_1_out_2 ? ramstick_4_p6 : 32'bz;  // Controlled_Buffer controlled_buffer_4
endmodule

module M32 (
  input  CLK,
  input  WT,
  input  [31:0] RAWIN,
  output RD,
  output WR,
  output [31:0] RAWOUT,
  output [29:0] AOUT,
  output [3:0] BEOUT
);

  wire branchunit_1_br, EN_A, EN_D, getcarry_1_carry, RD_DEST, SEL_D, SEL_REG, unifiedwire_1_p1;
  wire [1:0] geta1a0_1_a1a0, OP_ABI, OP_Y_SEL;
  wire [2:0] OP_DBI;
  wire [3:0] abi_1_beout, alu_1_zvsc, OP_ALU, sr_1_outpt;
  wire [4:0] unifiedwire_9_p1, unifiedwire_10_p1, unifiedwire_11_p1;
  wire [29:0] abi_1_aout;
  wire [31:0] ar_1_outpt, dbi_1_rawout, ir_1_outpt, muxm32_1_outpt, muxm32_2_outpt, unifiedwire_13_p1,
       ysel_1_y;
  wire [63:0] SIGNALS;

  // ControlUnitCycleMain controlunitcyclemain_1: pin names not known
  // UnifiedWire unifiedwire_1: pin names not known; wires that end beside it: unifiedwire_1_p1
  // UnifiedWire unifiedwire_2: pin names not known
  PC pc_1 (.CLK(CLK), .WR(SIGNALS[0]));  // open: INPT, OUTPT
  MUXM32 muxm32_1 (.SEL(SEL_REG), .OUTPT(muxm32_1_outpt));  // open: S0, S1
  // UnifiedWire unifiedwire_3: pin names not known; wires that end beside it: muxm32_1_outpt
  // UnifiedWire unifiedwire_4: pin names not known
  RBANK rbank_1 (.WR(SIGNALS[1]), .CLK(CLK));  // open: d, s1, s2, Rd, Rs1, Rs2
  // UnifiedWire unifiedwire_5: pin names not known
  ALU alu_1 (.Carry(getcarry_1_carry), .OP(OP_ALU), .ZVSC(alu_1_zvsc));  // open: YPrima, XPrima, Z
  MUXM32 muxm32_2 (.SEL(SEL_D), .OUTPT(muxm32_2_outpt));  // open: S0, S1
  // UnifiedWire unifiedwire_6: pin names not known; wires that end beside it: unifiedwire_1_p1
  // UnifiedWire unifiedwire_7: pin names not known
  YSEL ysel_1 (.INST(ir_1_outpt), .OPYSEL(OP_Y_SEL), .Y(ysel_1_y));  // open: REGS
  // UnifiedWire unifiedwire_8: pin names not known; wires that end beside it: ysel_1_y
  // UnifiedWire unifiedwire_9: pin names not known; wires that end beside it: unifiedwire_9_p1
  // UnifiedWire unifiedwire_10: pin names not known; wires that end beside it: unifiedwire_10_p1
  // UnifiedWire unifiedwire_11: pin names not known; wires that end beside it: unifiedwire_11_p1
  GetCarry getcarry_1 (.in_1(sr_1_outpt), .Carry(getcarry_1_carry));
  SR sr_1 (.WR_SR(SIGNALS[11]), .CLK(CLK), .INPT(alu_1_zvsc), .OUTPT(sr_1_outpt));
  // UnifiedWire unifiedwire_12: pin names not known; wires that end beside it: muxm32_2_outpt
  // Probe on sr_1_outpt
  // UnifiedWire unifiedwire_13: pin names not known; wires that end beside it: unifiedwire_13_p1
  // UnifiedWire unifiedwire_14: pin names not known
  // UnifiedWire unifiedwire_15: pin names not known; wires that end beside it: unifiedwire_1_p1
  RSEL rsel_1 (.I(ir_1_outpt), .RDDEST(RD_DEST), .s2(unifiedwire_10_p1), .s1(unifiedwire_9_p1), .d(unifiedwire_11_p1));
  BRANCHUNIT branchunit_1 (.OP(ir_1_outpt), .ZVSC(sr_1_outpt), .BR(branchunit_1_br));
  GetA1A0 geta1a0_1 (.I32(ar_1_outpt), .A1A0(geta1a0_1_a1a0));
  AR ar_1 (.WR_AR(SIGNALS[13]), .CLK(CLK), .OUTPT(ar_1_outpt));  // open: INPT
  // Probe on ar_1_outpt
  ControlUnit controlunit_1 (
    .WAIT_PIN(WT), .OP(ir_1_outpt), .BR(branchunit_1_br), .CLOCK(CLK),
    .SIGNALS({SIGNALS[63:23], WR, RD, EN_A, EN_D, OP_DBI, OP_ABI, SIGNALS[13], SEL_D, SIGNALS[11], OP_ALU, OP_Y_SEL, SEL_REG, SIGNALS[3], RD_DEST, SIGNALS[1:0]}));
  DBI dbi_1 (
    .A1A0(geta1a0_1_a1a0), .OP(OP_DBI), .RAWIN(RAWIN), .DIN(unifiedwire_13_p1), .RAWOUT(dbi_1_rawout));  // open: DOUT
  // UnifiedWire unifiedwire_16: pin names not known; wires that end beside it: unifiedwire_1_p1
  IR ir_1 (.WRIR(SIGNALS[3]), .CLOCK(CLK), .OUTPT(ir_1_outpt));  // open: INPT
  // Probe on ir_1_outpt
  ABI abi_1 (.AIN(ar_1_outpt), .OP(OP_ABI), .BEOUT(abi_1_beout), .AOUT(abi_1_aout));
  assign RAWOUT = EN_D ? dbi_1_rawout : 32'bz;  // Controlled_Buffer controlled_buffer_1
  assign AOUT = EN_A ? abi_1_aout : 30'bz;  // Controlled_Buffer controlled_buffer_2
  assign BEOUT = EN_A ? abi_1_beout : 4'bz;  // Controlled_Buffer controlled_buffer_3

  // Other names for the same wires on the sheet: WR_PC = SIGNALS[0]; WR_RD = SIGNALS[1];
  //   SIGNALS (some bits) = {WR, RD, EN_A, EN_D, OP_DBI, OP_ABI, SEL_D, OP_ALU, OP_Y_SEL, SEL_REG, RD_DEST};
  //   WR_IR = SIGNALS[3]; WR_SR = SIGNALS[11]; WR_AR = SIGNALS[13]
endmodule

module PC (
  input  [31:0] INPT,
  input  CLK,
  input  WR,
  output [31:0] OUTPT
);

  wire check_on_machine_1_addr_cero, wait3_1_wt;
  wire [31:0] register_1_q;

  Wait3 wait3_1 (.CLK(CLK), .WT(wait3_1_wt));
  Register #(.width(32)) register_1 (.D(INPT), .en(WR), .clk(CLK), .Q(register_1_q));  // open: clr
  Multiplexer #(.width(32)) multiplexer_1 (
    .in0({32{1'b0}}), .in1(register_1_q), .out(OUTPT), .sel(check_on_machine_1_addr_cero));
  Check_On_Machine check_on_machine_1 (
    .CLK(CLK), .WR(WR), .NRESET(wait3_1_wt), .ADDR_CERO(check_on_machine_1_addr_cero));

  // Notes on the sheet:
  //   El Contador de Programa (PC) es un registro de 32 bits que mantiene la dirección
  //   de la siguiente instrucción a ejecutar en la memoria del programa.
endmodule

module RBANK (
  input  [31:0] Rd,
  input  CLK,
  input  [4:0] s1,
  input  [4:0] s2,
  input  WR,
  input  [4:0] d,
  output [31:0] Rs1,
  output [31:0] Rs2
);

  wire decoder_1_out1, decoder_1_out2, decoder_1_out3, decoder_1_out4, decoder_1_out5, decoder_1_out6,
       decoder_1_out7, decoder_1_out8, decoder_1_out9, decoder_1_out10, decoder_1_out11, decoder_1_out12,
       decoder_1_out13, decoder_1_out14, decoder_1_out15, decoder_1_out16, decoder_1_out17, decoder_1_out18,
       decoder_1_out19, decoder_1_out20, decoder_1_out21, decoder_1_out22, decoder_1_out23, decoder_1_out24,
       decoder_1_out25, decoder_1_out26, decoder_1_out27, decoder_1_out28, decoder_1_out29, decoder_1_out30,
       decoder_1_out31;
  wire [31:0] register_1_q, register_2_q, register_3_q, register_4_q, register_5_q, register_6_q,
       register_7_q, register_8_q, register_9_q, register_10_q, register_11_q, register_12_q, register_13_q,
       register_14_q, register_15_q, register_16_q, register_17_q, register_18_q, register_19_q,
       register_20_q, register_21_q, register_22_q, register_23_q, register_24_q, register_25_q,
       register_26_q, register_27_q, register_28_q, register_29_q, register_30_q, register_31_q;

  Decoder #(.select(5)) decoder_1 (
    .out1(decoder_1_out1), .out2(decoder_1_out2), .out3(decoder_1_out3), .out4(decoder_1_out4),
    .out5(decoder_1_out5), .out6(decoder_1_out6), .out7(decoder_1_out7), .out8(decoder_1_out8),
    .out9(decoder_1_out9), .out10(decoder_1_out10), .out11(decoder_1_out11), .out12(decoder_1_out12),
    .out13(decoder_1_out13), .out14(decoder_1_out14), .out15(decoder_1_out15), .out16(decoder_1_out16),
    .out17(decoder_1_out17), .out18(decoder_1_out18), .out19(decoder_1_out19), .out20(decoder_1_out20),
    .out21(decoder_1_out21), .out22(decoder_1_out22), .out23(decoder_1_out23), .out24(decoder_1_out24),
    .out25(decoder_1_out25), .out26(decoder_1_out26), .out27(decoder_1_out27), .out28(decoder_1_out28),
    .out29(decoder_1_out29), .out30(decoder_1_out30), .out31(decoder_1_out31), .sel(d), .en(WR));  // open: out0
  Register #(.width(32)) register_1 (.D(Rd), .en(decoder_1_out1), .clk(CLK), .Q(register_1_q));  // open: clr
  Register #(.width(32)) register_2 (.D(Rd), .en(decoder_1_out2), .clk(CLK), .Q(register_2_q));  // open: clr
  Register #(.width(32)) register_3 (.D(Rd), .en(decoder_1_out3), .clk(CLK), .Q(register_3_q));  // open: clr
  Register #(.width(32)) register_4 (.D(Rd), .en(decoder_1_out4), .clk(CLK), .Q(register_4_q));  // open: clr
  Register #(.width(32)) register_5 (.D(Rd), .en(decoder_1_out5), .clk(CLK), .Q(register_5_q));  // open: clr
  Register #(.width(32)) register_6 (.D(Rd), .en(decoder_1_out6), .clk(CLK), .Q(register_6_q));  // open: clr
  Register #(.width(32)) register_7 (.D(Rd), .en(decoder_1_out7), .clk(CLK), .Q(register_7_q));  // open: clr
  Register #(.width(32)) register_8 (.D(Rd), .en(decoder_1_out8), .clk(CLK), .Q(register_8_q));  // open: clr
  Register #(.width(32)) register_9 (.D(Rd), .en(decoder_1_out9), .clk(CLK), .Q(register_9_q));  // open: clr
  Register #(.width(32)) register_10 (.D(Rd), .en(decoder_1_out10), .clk(CLK), .Q(register_10_q));  // open: clr
  Register #(.width(32)) register_11 (.D(Rd), .en(decoder_1_out11), .clk(CLK), .Q(register_11_q));  // open: clr
  Register #(.width(32)) register_12 (.D(Rd), .en(decoder_1_out12), .clk(CLK), .Q(register_12_q));  // open: clr
  Register #(.width(32)) register_13 (.D(Rd), .en(decoder_1_out13), .clk(CLK), .Q(register_13_q));  // open: clr
  Register #(.width(32)) register_14 (.D(Rd), .en(decoder_1_out14), .clk(CLK), .Q(register_14_q));  // open: clr
  Register #(.width(32)) register_15 (.D(Rd), .en(decoder_1_out15), .clk(CLK), .Q(register_15_q));  // open: clr
  Register #(.width(32)) register_16 (.D(Rd), .en(decoder_1_out16), .clk(CLK), .Q(register_16_q));  // open: clr
  Register #(.width(32)) register_17 (.D(Rd), .en(decoder_1_out17), .clk(CLK), .Q(register_17_q));  // open: clr
  Register #(.width(32)) register_18 (.D(Rd), .en(decoder_1_out18), .clk(CLK), .Q(register_18_q));  // open: clr
  Register #(.width(32)) register_19 (.D(Rd), .en(decoder_1_out19), .clk(CLK), .Q(register_19_q));  // open: clr
  Register #(.width(32)) register_20 (.D(Rd), .en(decoder_1_out20), .clk(CLK), .Q(register_20_q));  // open: clr
  Register #(.width(32)) register_21 (.D(Rd), .en(decoder_1_out21), .clk(CLK), .Q(register_21_q));  // open: clr
  Register #(.width(32)) register_22 (.D(Rd), .en(decoder_1_out22), .clk(CLK), .Q(register_22_q));  // open: clr
  Register #(.width(32)) register_23 (.D(Rd), .en(decoder_1_out23), .clk(CLK), .Q(register_23_q));  // open: clr
  Register #(.width(32)) register_24 (.D(Rd), .en(decoder_1_out24), .clk(CLK), .Q(register_24_q));  // open: clr
  Register #(.width(32)) register_25 (.D(Rd), .en(decoder_1_out25), .clk(CLK), .Q(register_25_q));  // open: clr
  Register #(.width(32)) register_26 (.D(Rd), .en(decoder_1_out26), .clk(CLK), .Q(register_26_q));  // open: clr
  Register #(.width(32)) register_27 (.D(Rd), .en(decoder_1_out27), .clk(CLK), .Q(register_27_q));  // open: clr
  Register #(.width(32)) register_28 (.D(Rd), .en(decoder_1_out28), .clk(CLK), .Q(register_28_q));  // open: clr
  Register #(.width(32)) register_29 (.D(Rd), .en(decoder_1_out29), .clk(CLK), .Q(register_29_q));  // open: clr
  Register #(.width(32)) register_30 (.D(Rd), .en(decoder_1_out30), .clk(CLK), .Q(register_30_q));  // open: clr
  Register #(.width(32)) register_31 (.D(Rd), .en(decoder_1_out31), .clk(CLK), .Q(register_31_q));  // open: clr
  Multiplexer #(.select(5), .width(32)) multiplexer_1 (
    .in0({32{1'b0}}), .in1(register_1_q), .in2(register_2_q), .in3(register_3_q), .in4(register_4_q),
    .in5(register_5_q), .in6(register_6_q), .in7(register_7_q), .in8(register_8_q), .in9(register_9_q),
    .in10(register_10_q), .in11(register_11_q), .in12(register_12_q), .in13(register_13_q),
    .in14(register_14_q), .in15(register_15_q), .in16(register_16_q), .in17(register_17_q),
    .in18(register_18_q), .in19(register_19_q), .in20(register_20_q), .in21(register_21_q),
    .in22(register_22_q), .in23(register_23_q), .in24(register_24_q), .in25(register_25_q),
    .in26(register_26_q), .in27(register_27_q), .in28(register_28_q), .in29(register_29_q),
    .in30(register_30_q), .in31(register_31_q), .out(Rs2), .sel(s2));
  Multiplexer #(.select(5), .width(32)) multiplexer_2 (
    .in0({32{1'b0}}), .in1(register_1_q), .in2(register_2_q), .in3(register_3_q), .in4(register_4_q),
    .in5(register_5_q), .in6(register_6_q), .in7(register_7_q), .in8(register_8_q), .in9(register_9_q),
    .in10(register_10_q), .in11(register_11_q), .in12(register_12_q), .in13(register_13_q),
    .in14(register_14_q), .in15(register_15_q), .in16(register_16_q), .in17(register_17_q),
    .in18(register_18_q), .in19(register_19_q), .in20(register_20_q), .in21(register_21_q),
    .in22(register_22_q), .in23(register_23_q), .in24(register_24_q), .in25(register_25_q),
    .in26(register_26_q), .in27(register_27_q), .in28(register_28_q), .in29(register_29_q),
    .in30(register_30_q), .in31(register_31_q), .out(Rs1), .sel(s1));

  // Notes on the sheet:
  //   El Banco de Registros es la implementación de un arreglo de registros, que sirven a su vez como registros de propósito general
  //   del procesador. Dicho arreglo se diseña como el conjunto de 32 palabras de 32 bits cada una (donde cada registro representa una
  //   palabra), permitiendo acceso simultáneo a múltiples registros en un mismo ciclo de reloj
endmodule

module BRANCHUNIT (
  input  [31:0] OP,
  input  [3:0] ZVSC,
  output BR
);

  wire and_1_out, and_2_out, and_3_out, and_4_out, and_5_out, and_6_out, and_7_out, and_8_out, and_9_out,
       and_10_out, and_11_out, and_12_out, and_13_out, and_14_out, and_15_out, and_16_out, and_17_out,
       not_1_out, not_2_out, not_3_out, not_4_out, or_1_out, or_2_out, or_3_out, or_4_out, or_5_out,
       or_6_out, or_7_out, selecsalto_1_q0, selecsalto_1_q1, selecsalto_1_q2, selecsalto_1_q3,
       selecsalto_1_q4, selecsalto_1_q5, selecsalto_1_q6, selecsalto_1_q7, selecsalto_1_q8, selecsalto_1_q9;

  SELECSALTO selecsalto_1 (
    .INPT(OP), .q0(selecsalto_1_q0), .q1(selecsalto_1_q1), .q2(selecsalto_1_q2), .q3(selecsalto_1_q3),
    .q4(selecsalto_1_q4), .q5(selecsalto_1_q5), .q6(selecsalto_1_q6), .q7(selecsalto_1_q7),
    .q8(selecsalto_1_q8), .q9(selecsalto_1_q9));
  not not_1 (not_1_out, ZVSC[3]);
  not not_2 (not_2_out, ZVSC[2]);
  not not_3 (not_3_out, ZVSC[1]);
  not not_4 (not_4_out, ZVSC[0]);
  and and_1 (and_1_out, ZVSC[0], selecsalto_1_q0);
  and and_2 (and_2_out, not_4_out, selecsalto_1_q1);
  and and_3 (and_3_out, not_3_out, not_2_out);
  and and_4 (and_4_out, ZVSC[1], ZVSC[2]);
  and and_5 (and_5_out, not_2_out, not_3_out);
  and and_6 (and_6_out, ZVSC[2], ZVSC[1]);
  and and_7 (and_7_out, not_2_out, ZVSC[1]);
  and and_8 (and_8_out, ZVSC[2], not_4_out, selecsalto_1_q4);
  and and_9 (and_9_out, not_2_out, ZVSC[1]);
  and and_10 (and_10_out, ZVSC[2], not_3_out);
  and and_11 (and_11_out, ZVSC[3], not_4_out, selecsalto_1_q6);
  and and_12 (and_12_out, ZVSC[3], selecsalto_1_q7);
  and and_13 (and_13_out, not_1_out, selecsalto_1_q8);
  or or_1 (or_1_out, not_1_out, ZVSC[0]);
  or or_2 (or_2_out, and_3_out, and_4_out);
  or or_3 (or_3_out, and_5_out, and_6_out);
  or or_4 (or_4_out, and_7_out, and_8_out);
  or or_5 (or_5_out, and_9_out, ZVSC[0], and_10_out);
  and and_14 (and_14_out, or_1_out, selecsalto_1_q9);
  and and_15 (and_15_out, or_2_out, not_4_out, selecsalto_1_q2);
  and and_16 (and_16_out, or_3_out, selecsalto_1_q3);
  and and_17 (and_17_out, or_5_out, selecsalto_1_q5);
  or or_6 (or_6_out, and_1_out, and_2_out, and_15_out, and_16_out);
  or or_7 (or_7_out, and_11_out, and_12_out, and_13_out, and_14_out);
  or or_8 (BR, or_6_out, or_4_out, and_17_out, or_7_out);

  // Notes on the sheet:
  //   La Unidad de Saltos evalúa las condiciones de salto y determina si debe ocurrir una redirección en el flujo de programa.
endmodule

module ABI (
  input  [31:0] AIN,
  input  [1:0] OP,
  output [29:0] AOUT,
  output [3:0] BEOUT
);

  wire and_1_out, and_2_out, and_3_out, and_4_out, and_5_out, and_6_out, and_7_out, and_8_out, and_9_out,
       and_10_out, not_1_out, not_2_out, not_3_out, not_4_out;

  not not_1 (not_1_out, OP[1]);
  not not_2 (not_2_out, OP[0]);
  not not_3 (not_3_out, AIN[1]);
  not not_4 (not_4_out, AIN[0]);
  and and_1 (and_1_out, not_1_out, not_2_out, not_3_out, not_4_out);
  and and_2 (and_2_out, not_1_out, OP[0], AIN[1], not_4_out);
  and and_3 (and_3_out, OP[1], not_2_out, AIN[1], AIN[0]);
  and and_4 (and_4_out, not_1_out, not_2_out, not_3_out, not_4_out);
  and and_5 (and_5_out, not_1_out, OP[0], AIN[1], not_4_out);
  and and_6 (and_6_out, OP[1], not_2_out, AIN[1], not_4_out);
  and and_7 (and_7_out, not_1_out, not_3_out, not_4_out);
  and and_8 (and_8_out, OP[1], not_2_out, not_3_out, AIN[0]);
  and and_9 (and_9_out, not_2_out, not_3_out, not_4_out);
  and and_10 (and_10_out, not_1_out, not_3_out, not_4_out);
  or or_1 (BEOUT[0], and_1_out, and_2_out, and_3_out);
  or or_2 (BEOUT[1], and_4_out, and_5_out, and_6_out);
  or or_3 (BEOUT[2], and_7_out, and_8_out);
  or or_4 (BEOUT[3], and_9_out, and_10_out);

  assign AIN[30] = AIN[31];
  assign AOUT = AIN[29:0];
  // also tied to GND on the sheet: AIN[31]

  // Notes on the sheet:
  //   de Direcciones (AR) hacia la memoria.
  //   Las Interfaces de Bus de Datos (DBI) y Dirección (ABI) constituyen la conexión entre el procesador y el sistema de
  //   memoria externo. La interfaz ABI es unidireccional de 32 bits, transmitiendo la dirección de memoria desde el Registro
endmodule

module ALU (
  input  [31:0] XPrima,
  input  [31:0] YPrima,
  input  Carry,
  input  [3:0] OP,
  output [31:0] Z,
  output [3:0] ZVSC
);

  wire subcarry_1_carryprima;
  wire [31:0] adder_1_out, and_1_out, or_1_out, sll_alu_1_z, sra_alu_1_z, srl_alu_1_z, subcarry_1_outpt,
       xor_1_out;

  SUBCARRY subcarry_1 (
    .YPrima(YPrima), .OP(OP), .Carry(Carry), .OUTPT(subcarry_1_outpt), .CarryPrima(subcarry_1_carryprima));
  assign xor_1_out = XPrima ^ subcarry_1_outpt;  // XOR_Gate xor_1, 32 bits wide
  assign or_1_out = XPrima | subcarry_1_outpt;  // OR_Gate or_1, 32 bits wide
  assign and_1_out = XPrima & subcarry_1_outpt;  // AND_Gate and_1, 32 bits wide
  Adder #(.width(32)) adder_1 (
    .a(XPrima), .b(subcarry_1_outpt), .out(adder_1_out), .cin(subcarry_1_carryprima), .cout(ZVSC[3]));
  SRA_ALU sra_alu_1 (.X(XPrima), .Y(subcarry_1_outpt), .Z(sra_alu_1_z));
  SRL_ALU srl_alu_1 (.X(XPrima), .Y(subcarry_1_outpt), .Z(srl_alu_1_z));
  SLL_ALU sll_alu_1 (.X(XPrima), .Y(subcarry_1_outpt), .Z(sll_alu_1_z));
  Multiplexer #(.select(4), .width(32)) multiplexer_1 (
    .in0(adder_1_out), .in1(adder_1_out), .in2(adder_1_out), .in3(adder_1_out), .in4(and_1_out),
    .in5(or_1_out), .in6(xor_1_out), .in7(sll_alu_1_z), .in8(srl_alu_1_z), .in9(sra_alu_1_z), .out(Z),
    .sel(OP));  // open: in10, in11, in12, in13, in14, in15
  NOR32 nor32_1 (.X(Z), .out_2(ZVSC[0]));

  assign ZVSC[2:1] = {Z[31], ZVSC[3]};

  // Notes on the sheet:
  //   aritmético-lógicas sobre datos de 32 bits.
  //   La Unidad Aritmético-Lógica es la responsable de ejecutar todas las operaciones
endmodule

module IR (
  input  [31:0] INPT,
  input  CLOCK,
  input  WRIR,
  output [31:0] OUTPT
);

  Register #(.width(32)) register_1 (.D(INPT), .en(WRIR), .clk(CLOCK), .Q(OUTPT));  // open: clr

  // Notes on the sheet:
  //   El Registro de Instrucciones almacena la instrucción actualmente en ejecución dentro del procesador.
endmodule

module RSEL (
  input  [31:0] I,
  input  RDDEST,
  output [4:0] d,
  output [4:0] s1,
  output [4:0] s2
);

  Multiplexer #(.width(5)) multiplexer_1 (.in0(I[18:14]), .in1(I[23:19]), .out(s1), .sel(RDDEST));

  assign d = I[23:19];
  assign s2 = I[12:8];

  // Notes on the sheet:
  //   El Selector de Registros es un componente decodificador que interpreta los campos de la instrucción para determinar qué
  //   registros del R-BANK deben ser accedidos en cada operación.
endmodule

module YSEL (
  input  [31:0] REGS,
  input  [31:0] INST,
  input  [1:0] OPYSEL,
  output [31:0] Y
);

  wire [31:0] multiplexer_1_out;

  Multiplexer #(.width(32)) multiplexer_1 (
    .in0(REGS), .in1({{20{INST[12]}}, INST[11:0]}), .out(multiplexer_1_out), .sel(INST[13]));
  Multiplexer #(.select(2), .width(32)) multiplexer_2 (
    .in0({32{1'b0}}), .in1(32'h4), .in2(multiplexer_1_out), .in3({{9{INST[23]}}, INST[22:0]}), .out(Y),
    .sel(OPYSEL));

  // Notes on the sheet:
  //   El Selector de Operando Y es un multiplexor que determina la fuente del segundo operador de la ALU.
endmodule

module SR (
  input  [3:0] INPT,
  input  WR_SR,
  input  CLK,
  output [3:0] OUTPT
);

  Register #(.width(4)) register_1 (.D(INPT), .en(WR_SR), .clk(CLK), .Q(OUTPT));  // open: clr

  // Notes on the sheet:
  //   El Registro de Estado almacena las banderas de condición generadas por la ALU, permitiendo que instrucciones posteriores
  //   tomen decisiones basadas en los resultados de cálculos previos
endmodule

module DBI (
  input  [31:0] RAWIN,
  input  [1:0] A1A0,
  input  [2:0] OP,
  input  [31:0] DOUT,
  output [31:0] DIN,
  output [31:0] RAWOUT
);

  wire op_dbi_select_1_o1, op_dbi_select_1_o2, op_dbi_select_1_o3, op_dbi_select_1_o4, op_dbi_select_1_o5,
       op_dbi_select_1_o6a, op_dbi_select_1_o6b, op_dbi_select_1_o6c, op_dbi_select_1_o6d,
       op_dbi_select_1_o7a, op_dbi_select_1_o7b, op_dbi_select_1_o7c, op_dbi_select_1_o7d,
       op_dbi_select_1_o8, op_dbi_select_1_o9a, op_dbi_select_1_o9b, op_dbi_select_1_o10a,
       op_dbi_select_1_o10b, op_dbi_select_1_o10c, op_dbi_select_1_o10d;

  OP_DBI_Select op_dbi_select_1 (
    .A1A0(A1A0), .OP(OP), .O1(op_dbi_select_1_o1), .O2(op_dbi_select_1_o2), .O3(op_dbi_select_1_o3),
    .O4(op_dbi_select_1_o4), .O5(op_dbi_select_1_o5), .O6a(op_dbi_select_1_o6a), .O6b(op_dbi_select_1_o6b),
    .O6c(op_dbi_select_1_o6c), .O6d(op_dbi_select_1_o6d), .O7a(op_dbi_select_1_o7a),
    .O7b(op_dbi_select_1_o7b), .O7c(op_dbi_select_1_o7c), .O7d(op_dbi_select_1_o7d), .O8(op_dbi_select_1_o8),
    .O9a(op_dbi_select_1_o9a), .O9b(op_dbi_select_1_o9b), .O10a(op_dbi_select_1_o10a),
    .O10b(op_dbi_select_1_o10b), .O10c(op_dbi_select_1_o10c), .O10d(op_dbi_select_1_o10d));
  assign DIN = op_dbi_select_1_o1 ? RAWIN : 32'bz;  // Controlled_Buffer controlled_buffer_1
  assign RAWOUT = op_dbi_select_1_o8 ? DOUT : 32'bz;  // Controlled_Buffer controlled_buffer_2
  HALF_WORD_Lee half_word_lee_1 (
    .RAWIN(RAWIN), .I2(op_dbi_select_1_o2), .I3(op_dbi_select_1_o3), .I4(op_dbi_select_1_o4),
    .I5(op_dbi_select_1_o5), .DIN(DIN));
  BYTE_Lee byte_lee_1 (
    .RAWIN(RAWIN), .I6a(op_dbi_select_1_o6a), .I6b(op_dbi_select_1_o6b), .I6c(op_dbi_select_1_o6c),
    .I6d(op_dbi_select_1_o6d), .I7a(op_dbi_select_1_o7a), .I7b(op_dbi_select_1_o7b),
    .I7c(op_dbi_select_1_o7c), .I7d(op_dbi_select_1_o7d), .DIN(DIN));
  HALF_WORD_Escribe half_word_escribe_1 (
    .DOUT(DOUT), .I1(op_dbi_select_1_o9a), .I2(op_dbi_select_1_o9b), .RAWOUT(RAWOUT));
  BYTE_Escribe byte_escribe_1 (
    .DOUT(DOUT), .I10a(op_dbi_select_1_o10a), .I10b(op_dbi_select_1_o10b), .I10c(op_dbi_select_1_o10c),
    .I10d(op_dbi_select_1_o10d), .RAWOUT(RAWOUT));

  // Notes on the sheet:
  //   Las Interfaces de Bus de Datos (DBI) y Dirección (ABI) constituyen la conexión entre el procesador y el sistema de
  //   memoria externo. La interfaz DBI también es bidireccional de 32 bits, transportando datos desde la memoria hacia el
  //   procesador durante operaciones de lectura, y desde el procesador hacia la memoria durante operaciones de escritura.
endmodule

module AR (
  input  [31:0] INPT,
  input  WR_AR,
  input  CLK,
  output [31:0] OUTPT
);

  Register #(.width(32)) register_1 (.D(INPT), .en(WR_AR), .clk(CLK), .Q(OUTPT));  // open: clr

  // Notes on the sheet:
  //   El Registro de Direcciones almacena la dirección de memoria a ser utilizada en operaciones de carga o almacenamiento de
  //   datos
endmodule

module MUXM32 (
  input  [31:0] S0,
  input  [31:0] S1,
  input  SEL,
  output [31:0] OUTPT
);

  Multiplexer #(.width(32)) multiplexer_1 (.in0(S0), .in1(S1), .out(OUTPT), .sel(SEL));
endmodule

module ControlUnit (
  input  [31:0] OP,
  input  BR,
  input  WAIT_PIN,
  input  CLOCK,
  output [63:0] SIGNALS
);

  wire [7:0] ADDR, optoaddr_1_nextop_addr;

  // ControlUnitCycle controlunitcycle_1: pin names not known; wires that end beside it: ADDR
  OpToAddr optoaddr_1 (
    .OP(OP), .EXECUTE(SIGNALS[23]), .NEXT_ADDR(SIGNALS[31:24]), .BR(BR), .WT(WAIT_PIN), .PrevAddr(ADDR),
    .NextOp_Addr(optoaddr_1_nextop_addr));
  Register register_1 (.D(optoaddr_1_nextop_addr), .en(1'b1), .clk(CLOCK), .Q(ADDR));  // open: clr
  ROM #(.dataWidth(64)) rom_1 (.addr(ADDR), .data(SIGNALS));

  // Notes on the sheet:
  //   de control especifica qué señales deben activarse en un determinado ciclo de reloj.
  //   La Unidad de Control es el componente más complejo del M32, responsable de generar la secuencia correcta de señales de
  //   control que coordinan todos los demás módulos del procesador. Su implementación se realiza mediante microprogramación,
  //   una técnica que almacena la lógica de control como un programa en una memoria ROM. Cada microinstrucción en la memoria
  //   contents of rom_1 (hex, n*v repeats v):
  //   1102280 2301008 3000000 4000021 800000 252 2d2 352 3d2 452 4d2 9d2 952 852 8d2 10000022 51 61 21
  //   1410a050 155f8194 0 17000000 0 19102050 1a5d0194 1b000000 0 1d102050 1e301002 1f000000 0 21106050
  //   22315002 23000000 0 2510a050 26339002 27000000 0 29106050 2a325002 2b000000 0 2d10a050 2e349002
  //   2f000000
endmodule

module OpToAddr (
  input  [31:0] OP,
  input  EXECUTE,
  input  [7:0] NEXT_ADDR,
  input  BR,
  input  WT,
  input  [7:0] PrevAddr,
  output [7:0] NextOp_Addr
);

  wire and_1_out, comparator_1_eq, comparator_1_gt, comparator_2_eq, comparator_2_lt, not_1_out, or_1_out,
       or_2_out;
  wire [7:0] adder_1_out, multiplexer_1_out, multiplexer_2_out, rom_1_data;

  ROM rom_1 (.addr(OP[31:24]), .data(rom_1_data));
  Comparator comparator_1 (.a(OP[31:24]), .b(8'h15), .gt(comparator_1_gt), .eq(comparator_1_eq));  // open: lt
  Comparator comparator_2 (.a(OP[31:24]), .b(8'h1e), .eq(comparator_2_eq), .lt(comparator_2_lt));  // open: gt
  not not_1 (not_1_out, BR);
  Adder adder_1 (.a(rom_1_data), .b(8'h1), .out(adder_1_out));  // open: cin, cout
  or or_1 (or_1_out, comparator_1_gt, comparator_1_eq);
  or or_2 (or_2_out, comparator_2_eq, comparator_2_lt);
  Multiplexer #(.width(8)) multiplexer_1 (
    .in0(rom_1_data), .in1(adder_1_out), .out(multiplexer_1_out), .sel(and_1_out));
  and and_1 (and_1_out, or_1_out, or_2_out, not_1_out);
  Multiplexer #(.width(8)) multiplexer_2 (
    .in0(NEXT_ADDR), .in1(multiplexer_1_out), .out(multiplexer_2_out), .sel(EXECUTE));
  Multiplexer #(.width(8)) multiplexer_3 (.in0(multiplexer_2_out), .in1(PrevAddr), .out(NextOp_Addr), .sel(WT));

  // Notes on the sheet:
  //   contents of rom_1 (hex, n*v repeats v):
  //   0 1c 20 24 28 2c 18 16 13 d e c b 5 6 7 8 9 a f 11*11
endmodule

module SELECSALTO (
  input  [31:0] INPT,
  output q0,
  output q1,
  output q2,
  output q3,
  output q4,
  output q5,
  output q6,
  output q7,
  output q8,
  output q9
);

  wire and_1_out, and_2_out, and_3_out, and_4_out, and_5_out, and_6_out, and_7_out, and_8_out, and_9_out,
       and_10_out, not_1_out, not_2_out, not_3_out, not_4_out;

  CHIPSELEC chipselec_1 (.A(INPT));  // open: OUTP
  not not_1 (not_1_out, INPT[27]);
  not not_2 (not_2_out, INPT[26]);
  not not_3 (not_3_out, INPT[25]);
  not not_4 (not_4_out, INPT[24]);
  and and_1 (and_1_out, INPT[24], not_3_out, INPT[26], not_1_out);
  and and_2 (and_2_out, not_4_out, INPT[25], INPT[26], not_1_out);
  and and_3 (and_3_out, INPT[24], INPT[25], INPT[26], not_1_out);
  and and_4 (and_4_out, not_4_out, not_3_out, not_2_out, INPT[27]);
  and and_5 (and_5_out, INPT[24], not_3_out, not_2_out, INPT[27]);
  and and_6 (and_6_out, not_4_out, INPT[25], not_2_out, INPT[27]);
  and and_7 (and_7_out, INPT[24], INPT[25], not_2_out, INPT[27]);
  and and_8 (and_8_out, not_4_out, not_3_out, INPT[26], INPT[27]);
  and and_9 (and_9_out, INPT[24], not_3_out, INPT[26], INPT[27]);
  and and_10 (and_10_out, not_4_out, INPT[25], INPT[26], INPT[27]);
  and and_11 (q0, and_1_out, 1'b1, INPT[28]);
  and and_12 (q1, 1'b1, and_2_out, INPT[28]);
  and and_13 (q2, and_3_out, 1'b1, INPT[28]);
  and and_14 (q3, and_4_out, 1'b1, INPT[28]);
  and and_15 (q4, and_5_out, 1'b1, INPT[28]);
  and and_16 (q5, and_6_out, 1'b1, INPT[28]);
  and and_17 (q6, and_7_out, 1'b1, INPT[28]);
  and and_18 (q7, and_8_out, 1'b1, INPT[28]);
  and and_19 (q8, and_9_out, 1'b1, INPT[28]);
  and and_20 (q9, and_10_out, 1'b1, INPT[28]);
endmodule

module CHIPSELEC (
  input  [31:0] A,
  output OUTP
);

  nor nor_1 (OUTP, A[5], A[6], A[7], A[8], A[9], A[10], A[11], A[12], A[13], A[14], A[15], A[16], A[17], A[18], A[19], A[20], A[21], A[22], A[23], A[24], A[25], A[26], A[27], A[28], A[29], A[30], A[31]);
endmodule

module SUBCARRY (
  input  [31:0] YPrima,
  input  [3:0] OP,
  input  Carry,
  output [31:0] OUTPT,
  output CarryPrima
);

  wire check_1_carry, check_1_sub;
  wire [31:0] adder_1_out, not_1_out;

  assign not_1_out = ~YPrima;  // NOT_Gate not_1, 32 bits wide
  Adder #(.width(32)) adder_1 (.a(not_1_out), .b(32'h1), .out(adder_1_out));  // open: cin, cout
  CHECK check_1 (.INPT(OP), .SUB(check_1_sub), .CARRY(check_1_carry));
  Multiplexer #(.width(32)) multiplexer_1 (.in0(YPrima), .in1(adder_1_out), .out(OUTPT), .sel(check_1_sub));
  and and_1 (CarryPrima, check_1_carry, Carry);
endmodule

module CHECK (
  input  [3:0] INPT,
  output SUB,
  output CARRY
);

  wire not_1_out, not_2_out;

  not not_1 (not_1_out, INPT[3]);
  not not_2 (not_2_out, INPT[2]);
  and and_1 (SUB, INPT[1], not_2_out, not_1_out);
  and and_2 (CARRY, INPT[0], not_2_out, not_1_out);
endmodule

module SRA_ALU (
  input  [31:0] X,
  input  [31:0] Y,
  output [31:0] Z
);

  wire [31:0] sra2_1_y, sra4_1_y, sra8_1_y, sra16_1_y;

  SRA16 sra16_1 (.X(X), .Enable(Y[4]), .Y(sra16_1_y));
  SRA8 sra8_1 (.X(sra16_1_y), .Enable(Y[3]), .Y(sra8_1_y));
  SRA4 sra4_1 (.X(sra8_1_y), .Enable(Y[2]), .Y(sra4_1_y));
  SRA2 sra2_1 (.X(sra4_1_y), .Enable(Y[1]), .Y(sra2_1_y));
  SRA1 sra1_1 (.X(sra2_1_y), .Enable(Y[0]), .Y(Z));
endmodule

module SRL_ALU (
  input  [31:0] X,
  input  [31:0] Y,
  output [31:0] Z
);

  wire [31:0] srl2_1_y, srl4_1_y, srl8_1_y, srl16_1_y;

  SRL16 srl16_1 (.X(X), .Enable(Y[4]), .Y(srl16_1_y));
  SRL8 srl8_1 (.X(srl16_1_y), .Enable(Y[3]), .Y(srl8_1_y));
  SRL4 srl4_1 (.X(srl8_1_y), .Enable(Y[2]), .Y(srl4_1_y));
  SRL2 srl2_1 (.X(srl4_1_y), .Enable(Y[1]), .Y(srl2_1_y));
  SRL1 srl1_1 (.X(srl2_1_y), .Enable(Y[0]), .Y(Z));
endmodule

module SLL_ALU (
  input  [31:0] X,
  input  [31:0] Y,
  output [31:0] Z
);

  wire [31:0] sll2_1_y, sll4_1_y, sll8_1_y, sll16_1_y;

  SLL16 sll16_1 (.X(X), .Enable(Y[4]), .Y(sll16_1_y));
  SLL8 sll8_1 (.X(sll16_1_y), .Enable(Y[3]), .Y(sll8_1_y));
  SLL4 sll4_1 (.X(sll8_1_y), .Enable(Y[2]), .Y(sll4_1_y));
  SLL2 sll2_1 (.X(sll4_1_y), .Enable(Y[1]), .Y(sll2_1_y));
  SLL1 sll1_1 (.X(sll2_1_y), .Enable(Y[0]), .Y(Z));
endmodule

module SRA16 (
  input  [31:0] X,
  input  Enable,
  output [31:0] Y
);

  SRAX srax_1 (.X(X), .COUNT(5'b10000), .Enable(Enable), .OUTPT(Y));
endmodule

module SRA8 (
  input  [31:0] X,
  input  Enable,
  output [31:0] Y
);

  SRAX srax_1 (.X(X), .COUNT(5'b01000), .Enable(Enable), .OUTPT(Y));
endmodule

module SRA4 (
  input  [31:0] X,
  input  Enable,
  output [31:0] Y
);

  SRAX srax_1 (.X(X), .COUNT(5'b00100), .Enable(Enable), .OUTPT(Y));
endmodule

module SRA2 (
  input  [31:0] X,
  input  Enable,
  output [31:0] Y
);

  SRAX srax_1 (.X(X), .COUNT(5'b00010), .Enable(Enable), .OUTPT(Y));
endmodule

module SRA1 (
  input  [31:0] X,
  input  Enable,
  output [31:0] Y
);

  SRAX srax_1 (.X(X), .COUNT(5'b00001), .Enable(Enable), .OUTPT(Y));
endmodule

module SRL16 (
  input  [31:0] X,
  input  Enable,
  output [31:0] Y
);

  SRLX srlx_1 (.X(X), .COUNT(5'b10000), .Enable(Enable), .OUTPT(Y));
endmodule

module SRL8 (
  input  [31:0] X,
  input  Enable,
  output [31:0] Y
);

  SRLX srlx_1 (.X(X), .COUNT(5'b01000), .Enable(Enable), .OUTPT(Y));
endmodule

module SRL4 (
  input  [31:0] X,
  input  Enable,
  output [31:0] Y
);

  SRLX srlx_1 (.X(X), .COUNT(5'b00100), .Enable(Enable), .OUTPT(Y));
endmodule

module SRL2 (
  input  [31:0] X,
  input  Enable,
  output [31:0] Y
);

  SRLX srlx_1 (.X(X), .COUNT(5'b00010), .Enable(Enable), .OUTPT(Y));
endmodule

module SRL1 (
  input  [31:0] X,
  input  Enable,
  output [31:0] Y
);

  SRLX srlx_1 (.X(X), .COUNT(5'b00001), .Enable(Enable), .OUTPT(Y));
endmodule

module SLL16 (
  input  [31:0] X,
  input  Enable,
  output [31:0] Y
);

  SLLX sllx_1 (.X(X), .COUNT(5'b10000), .Enable(Enable), .OUTPT(Y));
endmodule

module SLL8 (
  input  [31:0] X,
  input  Enable,
  output [31:0] Y
);

  SLLX sllx_1 (.X(X), .COUNT(5'b01000), .Enable(Enable), .OUTPT(Y));
endmodule

module SLL4 (
  input  [31:0] X,
  input  Enable,
  output [31:0] Y
);

  SLLX sllx_1 (.X(X), .COUNT(5'b00100), .Enable(Enable), .OUTPT(Y));
endmodule

module SLL2 (
  input  [31:0] X,
  input  Enable,
  output [31:0] Y
);

  SLLX sllx_1 (.X(X), .COUNT(5'b00010), .Enable(Enable), .OUTPT(Y));
endmodule

module SLL1 (
  input  [31:0] X,
  input  Enable,
  output [31:0] Y
);

  SLLX sllx_1 (.X(X), .COUNT(5'b00001), .Enable(Enable), .OUTPT(Y));
endmodule

module SRAX (
  input  [31:0] X,
  input  [4:0] COUNT,
  input  Enable,
  output [31:0] OUTPT
);

  wire [31:0] shifter_1_out;

  Shifter #(.shift("ar"), .width(32)) shifter_1 (.in(X), .\dist (COUNT), .out(shifter_1_out));
  Multiplexer #(.width(32)) multiplexer_1 (.in0(X), .in1(shifter_1_out), .out(OUTPT), .sel(Enable));
endmodule

module SRLX (
  input  [31:0] X,
  input  [4:0] COUNT,
  input  Enable,
  output [31:0] OUTPT
);

  wire [31:0] shifter_1_out;

  Shifter #(.shift("lr"), .width(32)) shifter_1 (.in(X), .\dist (COUNT), .out(shifter_1_out));
  Multiplexer #(.width(32)) multiplexer_1 (.in0(X), .in1(shifter_1_out), .out(OUTPT), .sel(Enable));
endmodule

module SLLX (
  input  [31:0] X,
  input  [4:0] COUNT,
  input  Enable,
  output [31:0] OUTPT
);

  wire [31:0] shifter_1_out;

  Shifter #(.width(32)) shifter_1 (.in(X), .\dist (COUNT), .out(shifter_1_out));
  Multiplexer #(.width(32)) multiplexer_1 (.in0(X), .in1(shifter_1_out), .out(OUTPT), .sel(Enable));
endmodule

module NOR32 (
  input  [31:0] X,
  output out_2
);

  nor nor_1 (out_2, X[0], X[1], X[2], X[3], X[4], X[5], X[6], X[7], X[8], X[9], X[10], X[11], X[12], X[13], X[14], X[15], X[16], X[17], X[18], X[19], X[20], X[21], X[22], X[23], X[24], X[25], X[26], X[27], X[28], X[29], X[30], X[31]);
endmodule

module Check_On_Machine (
  input  CLK,
  input  WR,
  input  NRESET,
  output ADDR_CERO
);

  wire d_ff_1_q, or_1_out;

  D_Flip_Flop d_ff_1 (.D(or_1_out), .clk(CLK), .Q(d_ff_1_q));  // open: Qn, preset, reset
  or or_1 (or_1_out, d_ff_1_q, WR);
  Multiplexer multiplexer_1 (.in0(1'b0), .in1(or_1_out), .out(ADDR_CERO), .sel(NRESET));
endmodule

module Wait3 (
  input  CLK,
  output WT
);

  wire comparator_1_eq, comparator_1_gt, not_1_out;
  wire [7:0] adder_1_out, register_1_q;

  Register register_1 (.D(adder_1_out), .en(not_1_out), .clk(CLK), .Q(register_1_q));  // open: clr
  Adder adder_1 (.a(register_1_q), .b(8'h1), .out(adder_1_out));  // open: cin, cout
  Comparator comparator_1 (.a(register_1_q), .b(8'h3), .gt(comparator_1_gt), .eq(comparator_1_eq));  // open: lt
  or or_1 (WT, comparator_1_gt, comparator_1_eq);
  not not_1 (not_1_out, WT);
endmodule

module OP_DBI_Select (
  input  [1:0] A1A0,
  input  [2:0] OP,
  output O1,
  output O2,
  output O3,
  output O4,
  output O5,
  output O6a,
  output O6b,
  output O6c,
  output O6d,
  output O7a,
  output O7b,
  output O7c,
  output O7d,
  output O8,
  output O9a,
  output O9b,
  output O10a,
  output O10b,
  output O10c,
  output O10d
);

  wire and_1_out, and_2_out, and_3_out, and_4_out, and_5_out, and_6_out, and_7_out, and_8_out, and_9_out,
       and_10_out, and_11_out, and_12_out, and_13_out, and_14_out, and_15_out, and_16_out, and_17_out,
       and_18_out, and_19_out, and_20_out, and_21_out, and_22_out, and_23_out, and_24_out, and_25_out,
       and_26_out, and_27_out, and_28_out, and_29_out, and_30_out, and_31_out, and_32_out, and_33_out,
       and_34_out, and_35_out, and_36_out, and_37_out, and_38_out, and_39_out, and_40_out, not_1_out,
       not_2_out, not_3_out, not_4_out, not_5_out;

  not not_1 (not_1_out, OP[2]);
  not not_2 (not_2_out, OP[1]);
  not not_3 (not_3_out, OP[0]);
  not not_4 (not_4_out, A1A0[1]);
  not not_5 (not_5_out, A1A0[0]);
  and and_1 (and_1_out, not_1_out, not_2_out);
  and and_2 (and_2_out, not_3_out, not_4_out, not_5_out);
  and and_3 (and_3_out, not_1_out, not_2_out);
  and and_4 (and_4_out, OP[0], not_4_out, not_5_out);
  and and_5 (and_5_out, not_1_out, not_2_out);
  and and_6 (and_6_out, OP[0], A1A0[1], not_5_out);
  and and_7 (and_7_out, not_1_out, OP[1]);
  and and_8 (and_8_out, not_3_out, not_4_out, not_5_out);
  and and_9 (and_9_out, not_1_out, OP[1]);
  and and_10 (and_10_out, not_3_out, A1A0[1], not_5_out);
  and and_11 (and_11_out, not_1_out, OP[1]);
  and and_12 (and_12_out, OP[0], not_4_out, not_5_out);
  and and_13 (and_13_out, not_1_out, OP[1]);
  and and_14 (and_14_out, OP[0], not_4_out, A1A0[0]);
  and and_15 (and_15_out, not_1_out, OP[1]);
  and and_16 (and_16_out, OP[0], A1A0[1], not_5_out);
  and and_17 (and_17_out, not_1_out, OP[1]);
  and and_18 (and_18_out, OP[0], A1A0[1], A1A0[0]);
  and and_19 (and_19_out, OP[2], not_2_out);
  and and_20 (and_20_out, not_3_out, not_4_out, not_5_out);
  and and_21 (and_21_out, OP[2], not_2_out);
  and and_22 (and_22_out, not_3_out, not_4_out, A1A0[0]);
  and and_23 (and_23_out, OP[2], not_2_out);
  and and_24 (and_24_out, not_3_out, A1A0[1], not_5_out);
  and and_25 (and_25_out, OP[2], not_2_out);
  and and_26 (and_26_out, not_3_out, A1A0[1], A1A0[0]);
  and and_27 (and_27_out, OP[2], not_2_out);
  and and_28 (and_28_out, OP[0], not_4_out, not_5_out);
  and and_29 (and_29_out, OP[2], OP[1]);
  and and_30 (and_30_out, not_3_out, not_4_out, not_5_out);
  and and_31 (and_31_out, OP[2], not_1_out);
  and and_32 (and_32_out, not_3_out, A1A0[1], not_5_out);
  and and_33 (and_33_out, OP[2], OP[1]);
  and and_34 (and_34_out, OP[0], not_4_out, not_5_out);
  and and_35 (and_35_out, OP[2], OP[1]);
  and and_36 (and_36_out, OP[0], not_4_out, A1A0[0]);
  and and_37 (and_37_out, OP[2], OP[1]);
  and and_38 (and_38_out, OP[0], A1A0[1], not_5_out);
  and and_39 (and_39_out, OP[2], OP[1]);
  and and_40 (and_40_out, OP[0], A1A0[1], A1A0[0]);
  and and_41 (O1, and_1_out, and_2_out);
  and and_42 (O2, and_3_out, and_4_out);
  and and_43 (O3, and_5_out, and_6_out);
  and and_44 (O4, and_7_out, and_8_out);
  and and_45 (O5, and_9_out, and_10_out);
  and and_46 (O6a, and_11_out, and_12_out);
  and and_47 (O6b, and_13_out, and_14_out);
  and and_48 (O6c, and_15_out, and_16_out);
  and and_49 (O6d, and_17_out, and_18_out);
  and and_50 (O7a, and_19_out, and_20_out);
  and and_51 (O7b, and_21_out, and_22_out);
  and and_52 (O7c, and_23_out, and_24_out);
  and and_53 (O7d, and_25_out, and_26_out);
  and and_54 (O8, and_27_out, and_28_out);
  and and_55 (O9a, and_29_out, and_30_out);
  and and_56 (O9b, and_31_out, and_32_out);
  and and_57 (O10a, and_33_out, and_34_out);
  and and_58 (O10b, and_35_out, and_36_out);
  and and_59 (O10c, and_37_out, and_38_out);
  and and_60 (O10d, and_39_out, and_40_out);
endmodule

module HALF_WORD_Lee (
  input  [31:0] RAWIN,
  input  I2,
  input  I3,
  input  I4,
  input  I5,
  output [31:0] DIN
);

  wire [31:31] not_1_out, not_2_out;

  not not_1 (not_1_out[31], I2);
  not not_2 (not_2_out[31], I3);
  assign DIN = I2 ? {{16{not_1_out[31]}}, RAWIN[31:16]} : 32'bz;  // Controlled_Buffer controlled_buffer_1
  assign DIN = I3 ? {{16{not_2_out[31]}}, RAWIN[15:0]} : 32'bz;  // Controlled_Buffer controlled_buffer_2
  assign DIN = I4 ? {{17{RAWIN[31]}}, RAWIN[30:16]} : 32'bz;  // Controlled_Buffer controlled_buffer_3
  assign DIN = I5 ? {{17{RAWIN[15]}}, RAWIN[14:0]} : 32'bz;  // Controlled_Buffer controlled_buffer_4
endmodule

module HALF_WORD_Escribe (
  input  [31:0] DOUT,
  input  I1,
  input  I2,
  output [31:0] RAWOUT
);

  wire [31:31] not_1_out, not_2_out;

  not not_1 (not_1_out[31], I1);
  not not_2 (not_2_out[31], I2);
  assign RAWOUT = I1 ? {{16{not_1_out[31]}}, DOUT[31:16]} : 32'bz;  // Controlled_Buffer controlled_buffer_1
  assign RAWOUT = I1 ? {{16{not_2_out[31]}}, DOUT[15:0]} : 32'bz;  // Controlled_Buffer controlled_buffer_2
endmodule

module BYTE_Lee (
  input  [31:0] RAWIN,
  input  I6a,
  input  I6b,
  input  I6c,
  input  I6d,
  input  I7a,
  input  I7b,
  input  I7c,
  input  I7d,
  output [31:0] DIN
);

  wire [31:31] not_1_out, not_2_out, not_3_out, not_4_out;

  not not_1 (not_1_out[31], I6a);
  not not_2 (not_2_out[31], I6b);
  not not_3 (not_3_out[31], I6c);
  not not_4 (not_4_out[31], I6d);
  assign DIN = I6a ? {{24{not_1_out[31]}}, RAWIN[31:24]} : 32'bz;  // Controlled_Buffer controlled_buffer_1
  assign DIN = I6b ? {{24{not_2_out[31]}}, RAWIN[23:16]} : 32'bz;  // Controlled_Buffer controlled_buffer_2
  assign DIN = I6c ? {{24{not_3_out[31]}}, RAWIN[15:8]} : 32'bz;  // Controlled_Buffer controlled_buffer_3
  assign DIN = I6d ? {{24{not_4_out[31]}}, RAWIN[7:0]} : 32'bz;  // Controlled_Buffer controlled_buffer_4
  assign DIN = I7a ? {{25{RAWIN[31]}}, RAWIN[30:24]} : 32'bz;  // Controlled_Buffer controlled_buffer_5
  assign DIN = I7b ? {{25{RAWIN[23]}}, RAWIN[22:16]} : 32'bz;  // Controlled_Buffer controlled_buffer_6
  assign DIN = I7c ? {{25{RAWIN[15]}}, RAWIN[14:8]} : 32'bz;  // Controlled_Buffer controlled_buffer_7
  assign DIN = I7d ? {{25{RAWIN[7]}}, RAWIN[6:0]} : 32'bz;  // Controlled_Buffer controlled_buffer_8
endmodule

module BYTE_Escribe (
  input  [31:0] DOUT,
  input  I10a,
  input  I10b,
  input  I10c,
  input  I10d,
  output [31:0] RAWOUT
);

  wire [31:31] not_1_out, not_2_out, not_3_out, not_4_out;

  not not_1 (not_1_out[31], I10a);
  not not_2 (not_2_out[31], I10b);
  not not_3 (not_3_out[31], I10c);
  not not_4 (not_4_out[31], I10d);
  assign RAWOUT = I10a ? {{24{not_1_out[31]}}, DOUT[31:24]} : 32'bz;  // Controlled_Buffer controlled_buffer_1
  assign RAWOUT = I10b ? {{24{not_2_out[31]}}, DOUT[23:16]} : 32'bz;  // Controlled_Buffer controlled_buffer_2
  assign RAWOUT = I10c ? {{24{not_3_out[31]}}, DOUT[15:8]} : 32'bz;  // Controlled_Buffer controlled_buffer_3
  assign RAWOUT = I10d ? {{24{not_4_out[31]}}, DOUT[7:0]} : 32'bz;  // Controlled_Buffer controlled_buffer_4
endmodule

module LoHiJoin64 (
  input  [63:0] INPT,
  output [63:0] out_2
);


  assign out_2 = {{48{1'b0}}, INPT[60], INPT[56], INPT[52], INPT[48], INPT[44], INPT[40], INPT[36], INPT[32], INPT[28], INPT[24], INPT[20], INPT[16], INPT[12], INPT[8], INPT[4], INPT[0]};
endmodule

module GetCarry (
  input  [3:0] in_1,
  output Carry
);


  assign Carry = in_1[3];
endmodule

module GetA1A0 (
  input  [31:0] I32,
  output [1:0] A1A0
);


  assign A1A0 = I32[1:0];
endmodule

module RAM_M32 (
  input  [31:0] Ain,
  input  [3:0] B3B0,
  input  WR,
  input  RD,
  input  CLK,
  input  [31:0] Din,
  output WT,
  output [31:0] Dout
);

  wire chipselectram_1_cs, comparator_1_eq, comparator_2_eq, comparator_2_gt, comparator_2_lt, not_1_out,
       or_1_out;
  wire [7:0] adder_1_out, multiplexer_1_out, multiplexer_2_out, multiplexer_3_out, multiplexer_4_out,
       ram_1_dout, ram_1_dout_2, ram_1_dout_3, ram_1_dout_4, register_1_q;
  wire [31:0] bit_extender_1_out, bit_extender_2_out, bit_extender_3_out, bit_extender_4_out, shifter_1_out,
       shifter_2_out, shifter_3_out, shifter_4_out, shifter_5_out;

  Shifter #(.shift("lr"), .width(32)) shifter_1 (.in(Ain), .\dist (5'b00010), .out(shifter_1_out));
  RAM #(.addrWidth(21), .dataWidth(32)) ram_1 (
    .addr(shifter_1_out[20:0]), .we(WR), .oe(RD), .clk(CLK), .din(Din),
    .dout({ram_1_dout, ram_1_dout_2, ram_1_dout_3, ram_1_dout_4}));
  Multiplexer #(.width(8)) multiplexer_1 (.in0({8{1'b0}}), .in1(ram_1_dout), .out(multiplexer_1_out), .sel(B3B0[3]));
  Multiplexer #(.width(8)) multiplexer_2 (.in0({8{1'b0}}), .in1(ram_1_dout_2), .out(multiplexer_2_out), .sel(B3B0[2]));
  CHIPSELECTRAM chipselectram_1 (.A31A23(shifter_1_out[31:23]), .RD(RD), .WR(WR), .CS(chipselectram_1_cs));
  Multiplexer #(.width(8)) multiplexer_3 (.in0({8{1'b0}}), .in1(ram_1_dout_3), .out(multiplexer_3_out), .sel(B3B0[1]));
  Adder adder_1 (.a(register_1_q), .b(8'h1), .out(adder_1_out));  // open: cin, cout
  Multiplexer #(.width(8)) multiplexer_4 (.in0({8{1'b0}}), .in1(ram_1_dout_4), .out(multiplexer_4_out), .sel(B3B0[0]));
  Register #(.trigger("falling")) register_1 (
    .D(adder_1_out), .en(chipselectram_1_cs), .clk(CLK), .Q(register_1_q), .clr(comparator_2_gt));
  assign bit_extender_1_out = {{24{1'b0}}, multiplexer_4_out};  // Bit_Extender bit_extender_1
  assign bit_extender_2_out = {{24{1'b0}}, multiplexer_3_out};  // Bit_Extender bit_extender_2
  assign bit_extender_3_out = {{24{1'b0}}, multiplexer_2_out};  // Bit_Extender bit_extender_3
  assign bit_extender_4_out = {{24{1'b0}}, multiplexer_1_out};  // Bit_Extender bit_extender_4
  Comparator comparator_1 (.a(register_1_q), .b({8{1'b0}}), .eq(comparator_1_eq));  // open: gt, lt
  Comparator comparator_2 (
    .a(register_1_q), .b(8'h3), .gt(comparator_2_gt), .eq(comparator_2_eq), .lt(comparator_2_lt));
  Shifter #(.width(32)) shifter_2 (.in(bit_extender_1_out), .\dist ({5{1'b0}}), .out(shifter_2_out));
  Shifter #(.width(32)) shifter_3 (.in(bit_extender_2_out), .\dist (5'b01000), .out(shifter_3_out));
  Shifter #(.width(32)) shifter_4 (.in(bit_extender_3_out), .\dist (5'b10000), .out(shifter_4_out));
  Shifter #(.width(32)) shifter_5 (.in(bit_extender_4_out), .\dist (5'b11000), .out(shifter_5_out));
  not not_1 (not_1_out, comparator_1_eq);
  or or_1 (or_1_out, comparator_2_eq, comparator_2_lt);
  assign Dout = shifter_2_out | shifter_3_out | shifter_4_out | shifter_5_out;  // OR_Gate or_2, 32 bits wide
  and and_1 (WT, not_1_out, or_1_out);
endmodule

module CHIPSELECTRAM (
  input  [8:0] A31A23,
  input  RD,
  input  WR,
  output CS
);

  wire nor_1_out, or_1_out;

  or or_1 (or_1_out, RD, WR);
  nor nor_1 (nor_1_out, A31A23[0], A31A23[1], A31A23[2], A31A23[3], A31A23[4], A31A23[5], A31A23[6], A31A23[7], A31A23[8]);
  and and_1 (CS, nor_1_out, or_1_out);
endmodule

module I30to32 (
  input  [29:0] INPT,
  output [31:0] OUTPT
);


  assign OUTPT = {2'b00, INPT};
endmodule

module SEL1 (
  input  [31:0] in_1,
  output out_2
);

  wire not_1_out, not_2_out, not_3_out, not_4_out, not_5_out, not_6_out, not_7_out, not_8_out, not_9_out,
       not_10_out, not_11_out, not_12_out, not_13_out;

  not not_1 (not_1_out, in_1[19]);
  not not_2 (not_2_out, in_1[20]);
  not not_3 (not_3_out, in_1[21]);
  not not_4 (not_4_out, in_1[22]);
  not not_5 (not_5_out, in_1[23]);
  not not_6 (not_6_out, in_1[24]);
  not not_7 (not_7_out, in_1[25]);
  not not_8 (not_8_out, in_1[26]);
  not not_9 (not_9_out, in_1[27]);
  not not_10 (not_10_out, in_1[28]);
  not not_11 (not_11_out, in_1[29]);
  not not_12 (not_12_out, in_1[30]);
  not not_13 (not_13_out, in_1[31]);
  and and_1 (out_2, not_1_out, not_2_out, not_3_out, not_4_out, not_5_out, not_6_out, not_7_out, not_8_out, not_9_out, not_10_out, not_11_out, not_12_out, not_13_out);
endmodule

module SEL2 (
  input  [31:0] in_1,
  output out_2
);

  wire not_1_out, not_2_out, not_3_out, not_4_out, not_5_out, not_6_out, not_7_out, not_8_out, not_9_out,
       not_10_out, not_11_out, not_12_out;

  not not_1 (not_1_out, in_1[20]);
  not not_2 (not_2_out, in_1[21]);
  not not_3 (not_3_out, in_1[22]);
  not not_4 (not_4_out, in_1[23]);
  not not_5 (not_5_out, in_1[24]);
  not not_6 (not_6_out, in_1[25]);
  not not_7 (not_7_out, in_1[26]);
  not not_8 (not_8_out, in_1[27]);
  not not_9 (not_9_out, in_1[28]);
  not not_10 (not_10_out, in_1[29]);
  not not_11 (not_11_out, in_1[30]);
  not not_12 (not_12_out, in_1[31]);
  and and_1 (out_2, in_1[19], not_1_out, not_2_out, not_3_out, not_4_out, not_5_out, not_6_out, not_7_out, not_8_out, not_9_out, not_10_out, not_11_out, not_12_out);
endmodule

module SEL3 (
  input  [31:0] in_1,
  output out_2
);

  wire not_1_out, not_2_out, not_3_out, not_4_out, not_5_out, not_6_out, not_7_out, not_8_out, not_9_out,
       not_10_out, not_11_out, not_12_out;

  not not_1 (not_1_out, in_1[19]);
  not not_2 (not_2_out, in_1[21]);
  not not_3 (not_3_out, in_1[22]);
  not not_4 (not_4_out, in_1[23]);
  not not_5 (not_5_out, in_1[24]);
  not not_6 (not_6_out, in_1[25]);
  not not_7 (not_7_out, in_1[26]);
  not not_8 (not_8_out, in_1[27]);
  not not_9 (not_9_out, in_1[28]);
  not not_10 (not_10_out, in_1[29]);
  not not_11 (not_11_out, in_1[30]);
  not not_12 (not_12_out, in_1[31]);
  and and_1 (out_2, not_1_out, in_1[20], not_2_out, not_3_out, not_4_out, not_5_out, not_6_out, not_7_out, not_8_out, not_9_out, not_10_out, not_11_out, not_12_out);
endmodule

module SEL4 (
  input  [31:0] in_1,
  output out_2
);

  wire not_1_out, not_2_out, not_3_out, not_4_out, not_5_out, not_6_out, not_7_out, not_8_out, not_9_out,
       not_10_out, not_11_out;

  not not_1 (not_1_out, in_1[21]);
  not not_2 (not_2_out, in_1[22]);
  not not_3 (not_3_out, in_1[23]);
  not not_4 (not_4_out, in_1[24]);
  not not_5 (not_5_out, in_1[25]);
  not not_6 (not_6_out, in_1[26]);
  not not_7 (not_7_out, in_1[27]);
  not not_8 (not_8_out, in_1[28]);
  not not_9 (not_9_out, in_1[29]);
  not not_10 (not_10_out, in_1[30]);
  not not_11 (not_11_out, in_1[31]);
  and and_1 (out_2, in_1[19], in_1[20], not_1_out, not_2_out, not_3_out, not_4_out, not_5_out, not_6_out, not_7_out, not_8_out, not_9_out, not_10_out, not_11_out);
endmodule
