// Logisim project RAM.circ as structural Verilog: 1 circuit, main circuit RAM_M32
module RAM_M32 (
  input  [31:0] Ain,
  input  WR,
  input  RD,
  input  CLK,
  input  [31:0] Din,
  output [31:0] Dout
);

  RAM #(.addrWidth(21), .dataWidth(32)) ram_1 (.addr(Ain[20:0]), .we(WR), .oe(RD), .clk(CLK), .din(Din), .dout(Dout));
endmodule
