// Logisim project Wait3.circ as structural Verilog: 1 circuit, main circuit Wait3
module Wait3 (
  input  CLK,
  output out_2
);

  wire comparator_1_eq, comparator_1_gt, not_1_out;
  wire [7:0] adder_1_out, register_1_q;

  Register register_1 (.D(adder_1_out), .en(not_1_out), .clk(CLK), .Q(register_1_q));  // open: clr
  Adder adder_1 (.a(register_1_q), .b(8'h1), .out(adder_1_out));  // open: cin, cout
  Comparator comparator_1 (.a(register_1_q), .b(8'h3), .gt(comparator_1_gt), .eq(comparator_1_eq));  // open: lt
  or or_1 (out_2, comparator_1_gt, comparator_1_eq);
  not not_1 (not_1_out, out_2);
endmodule
